// Logisim project CustomMultiplier.circ as structural Verilog: 1 circuit, main circuit CustomMultiplier
module CustomMultiplier (
  input  [7:0] FirstOperand,
  input  [7:0] SecondOperand,
  input  in_3,
  output [7:0] Result,
  output Done
);

  wire clk, counter_2_q, init_mode, shift_register_1_p1, shift_register_1_p3, shift_register_1_p6,
       shift_register_1_p16, shift_register_1_p18;
  wire [2:0] counter_1_q;
  wire [7:0] adder_1_out, and_1_out, shift_register_1_p21;
  wire [7:7] bitselector_1_out;

  Clock clock_1 (.out(clk));
  // Shift_Register shift_register_1: pin names not known; wires that end beside it: shift_register_1_p1, shift_register_1_p1, shift_register_1_p3, shift_register_1_p3, init_mode, shift_register_1_p6, clk, 1'b0, FirstOperand[0], FirstOperand[1], FirstOperand[2], FirstOperand[3], FirstOperand[4], FirstOperand[5], FirstOperand[7], shift_register_1_p16, shift_register_1_p16, shift_register_1_p18, shift_register_1_p18, FirstOperand[6], shift_register_1_p21[0], shift_register_1_p21[1], shift_register_1_p21[2], shift_register_1_p21[3], shift_register_1_p21[4], shift_register_1_p21[5], shift_register_1_p21[6], shift_register_1_p21[7]
  not not_1 (shift_register_1_p6, init_mode);
  Counter #(.max('hf), .width(4)) counter_1 (
    .clr(init_mode), .load(1'b0), .up(1'b1), .clk(clk), .Q({Done, counter_1_q}));  // open: count, D, carry
  Counter #(.max('h1), .width(1)) counter_2 (
    .load(1'b0), .up(1'b1), .count(init_mode), .clk(clk), .Q(counter_2_q));  // open: clr, D, carry
  BitSelector bitselector_1 (.in(SecondOperand), .out(bitselector_1_out[7]), .sel(counter_1_q));
  not not_2 (init_mode, counter_2_q);
  assign and_1_out = shift_register_1_p21 & {8{bitselector_1_out[7]}};  // AND_Gate and_1, 8 bits wide
  Adder adder_1 (.a(Result), .b(and_1_out), .out(adder_1_out));  // open: cin, cout
  Register register_1 (.D(adder_1_out), .en(1'b1), .clk(clk), .Q(Result));  // open: clr

  // Other names for the same wires on the sheet: A[7:0] = FirstOperand; B[7:0] = SecondOperand; C[7:0] = Result;
  //   clk1 = in_3
endmodule
